# Fritzing sketch Wiring (saved by Fritzing 0.9.5d)
breadboards: 1

parts:
  U1 = 74AHCT125 [part_number=SN74AHCT125 package=dil14]
  C1 = Capacitor Polarized [package=cpol-radial-100uf-25v]
  NEOPIXEL1 = Neopixel Strip -- Black (30/m) [part_number=1376]
  MCU1 = Raspberry Pi Zero  # not connected
  Part2 = Adafruit Pi Cobbler Plus [part_number="Adafruit #2029"]
  JACK1 = 2.1mm Barrel Jack with Terminal Block
  NEOPIXEL2 = Neopixel Strip -- Black (30/m) [part_number=1376]
  NEOPIXEL3 = Neopixel Strip -- Black (30/m) [part_number=1376]

nets:
  GND: U1.1OE, U1.GND, C1.-, NEOPIXEL1.GND, Part2.GND, JACK1.NEG, NEOPIXEL2.GND, NEOPIXEL3.GND
  N1: U1.1A, Part2.GPIO18
  N2: U1.1Y, NEOPIXEL1.Din
  +5V: U1.VCC, C1.+, NEOPIXEL1.+5V, JACK1.POS, NEOPIXEL2.+5V, NEOPIXEL3.+5V
  N3: NEOPIXEL1.Dout, NEOPIXEL2.Din
  N4: NEOPIXEL2.Dout, NEOPIXEL3.Din

custom parts:
  74AHCT125: Quad Level-Shifter (3V to 5V) Quadruple Bus Buffer Gates With 3-State Outputs
  Neopixel Strip -- Black (30/m): These NeoPixel strips have 30 digitally-addressable pixel LEDs per meter and are very affordable and are only 12.5 mm wide, 10 mm if you remove the strip from the casing.
  Adafruit Pi Cobbler Plus: The Raspberry Pi B+/Pi 2/ Pi 3 has landed on the Maker World like a 40-GPIO pinned, quad-USB ported, credit card sized bomb of DIY joy. And while you can use most of our great Model B accessories by hooking up our downgrade cable, its probably a good time to upgrade your set up and accessorize using all of the Model B+'s / Pi 2's / Pi 3's 40 pins. That's why we now carry the Adafruit Assembled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
